// Logisim project NanoSwitch16.circ as structural Verilog: 2 circuits, main circuit main
module main (
  input  [3:0] in_1,
  input  [3:0] in_2,
  output _0000,
  output _0010,
  output _0011,
  output _0100,
  output _0101,
  output _0110,
  output _0111,
  output _1000,
  output _1001,
  output _1010,
  output _1011,
  output _1100,
  output _1101,
  output _1110,
  output _1111
);

  wire adder_1_y, adder_2_x, adder_2_y, adder_3_x, adder_3_y, adder_4_x, adder_4_y, and_1_out, and_2_out,
       and_3_out, and_4_out, and_5_out, and_6_out, and_7_out, and_8_out, and_9_out, and_10_out, and_11_out,
       and_12_out, and_13_out, and_14_out, and_15_out, and_16_out, and_17_out, and_18_out, and_19_out,
       and_20_out, and_21_out, and_22_out, and_23_out, and_24_out, and_25_out, and_26_out, and_28_out,
       clock_1_out, d_ff_1_q, d_ff_2_q, d_ff_2_qn, d_ff_7_q, d_ff_7_qn, d_ff_12_q, d_ff_13_q, d_ff_14_q,
       d_ff_15_q, d_ff_16_q, d_ff_17_q, d_ff_18_q, d_ff_19_q, execute_puls_out, not_1_out, not_2_out,
       not_3_out, not_4_out, not_5_out, not_6_out, not_7_out, not_8_out, or_5_out, or_6_out, or_7_out,
       or_8_out;
  wire [3:0] d_ff_6_q, d_ff_20_q, or_1_out, or_9_out;
  wire [7:0] ram_1_dout;

  Clock clock_1 (.out(clock_1_out));
  and execute_puls (execute_puls_out, clock_1_out, d_ff_2_qn);
  not not_1 (not_1_out, d_ff_2_q);
  not not_2 (not_2_out, clock_1_out);
  D_Flip_Flop d_ff_1 (.D(and_28_out), .clk(not_2_out), .Q(d_ff_1_q));  // open: Qn, preset, reset
  D_Flip_Flop d_ff_2 (.D(not_1_out), .clk(clock_1_out), .Q(d_ff_2_q), .Qn(d_ff_2_qn));  // open: preset, reset
  and and_1 (and_1_out, d_ff_2_qn, d_ff_1_q, not_2_out);
  and and_2 (and_2_out, ram_1_dout[4], d_ff_7_q);
  and and_3 (and_3_out, ram_1_dout[5], d_ff_7_q);
  and and_4 (and_4_out, ram_1_dout[6], d_ff_7_q);
  and and_5 (and_5_out, ram_1_dout[7], d_ff_7_q);
  D_Flip_Flop d_ff_3 (.D(d_ff_12_q), .clk(d_ff_2_qn), .Q(d_ff_6_q[3]));  // open: Qn, preset, reset
  D_Flip_Flop d_ff_4 (.D(d_ff_13_q), .clk(d_ff_2_qn), .Q(d_ff_6_q[2]));  // open: Qn, preset, reset
  D_Flip_Flop d_ff_5 (.D(d_ff_14_q), .clk(d_ff_2_qn), .Q(d_ff_6_q[1]));  // open: Qn, preset, reset
  D_Flip_Flop d_ff_6 (.D(d_ff_15_q), .clk(d_ff_2_qn), .Q(d_ff_6_q[0]));  // open: Qn, preset, reset
  and and_6 (and_6_out, in_1[0], d_ff_2_q);
  and and_7 (and_7_out, in_1[1], d_ff_2_q);
  and and_8 (and_8_out, in_1[2], d_ff_2_q);
  and and_9 (and_9_out, in_1[3], d_ff_2_q);
  and and_10 (and_10_out, in_2[0], d_ff_2_qn);
  and and_11 (and_11_out, in_2[1], d_ff_2_qn);
  and and_12 (and_12_out, in_2[2], d_ff_2_qn);
  and and_13 (and_13_out, in_2[3], d_ff_2_qn);
  and and_14 (and_14_out, ram_1_dout[0], d_ff_7_qn);
  and and_15 (and_15_out, ram_1_dout[1], d_ff_7_qn);
  and and_16 (and_16_out, ram_1_dout[2], d_ff_7_qn);
  and and_17 (and_17_out, ram_1_dout[3], d_ff_7_qn);
  or or_1 (or_1_out[0], and_6_out, and_10_out);
  or or_2 (or_1_out[1], and_7_out, and_11_out);
  or or_3 (or_1_out[2], and_8_out, and_12_out);
  or or_4 (or_1_out[3], and_9_out, and_13_out);
  RAM ram_1 (.addr({or_1_out, or_9_out}), .oe(1'b1), .clk(clock_1_out), .dout(ram_1_dout));  // open: we, din
  D_Flip_Flop d_ff_7 (.Q(d_ff_7_q), .Qn(d_ff_7_qn));  // open: D, clk, preset, reset
  D_Flip_Flop d_ff_8 (.D(or_5_out), .clk(and_1_out));  // open: Q, Qn, preset, reset
  or or_5 (or_5_out, and_14_out, and_2_out);
  D_Flip_Flop d_ff_9 (.D(or_6_out), .clk(and_1_out));  // open: Q, Qn, preset, reset
  or or_6 (or_6_out, and_15_out, and_3_out);
  D_Flip_Flop d_ff_10 (.D(or_7_out), .clk(and_1_out));  // open: Q, Qn, preset, reset
  or or_7 (or_7_out, and_16_out, and_4_out);
  D_Flip_Flop d_ff_11 (.D(or_8_out), .clk(and_1_out));  // open: Q, Qn, preset, reset
  or or_8 (or_8_out, and_17_out, and_5_out);
  adder adder_1 (.a(d_ff_6_q[3]), .b(adder_2_x), .y(adder_1_y));  // open: x
  adder adder_2 (.a(d_ff_6_q[2]), .b(adder_3_x), .x(adder_2_x), .y(adder_2_y));
  adder adder_3 (.a(d_ff_6_q[1]), .b(adder_4_x), .x(adder_3_x), .y(adder_3_y));
  adder adder_4 (.a(d_ff_6_q[0]), .b(1'b1), .x(adder_4_x), .y(adder_4_y));
  not not_3 (not_3_out, clock_1_out);
  D_Flip_Flop d_ff_12 (.D(adder_1_y), .clk(clock_1_out), .Q(d_ff_12_q));  // open: Qn, preset, reset
  D_Flip_Flop d_ff_13 (.D(adder_2_y), .clk(clock_1_out), .Q(d_ff_13_q));  // open: Qn, preset, reset
  D_Flip_Flop d_ff_14 (.D(adder_3_y), .clk(clock_1_out), .Q(d_ff_14_q));  // open: Qn, preset, reset
  D_Flip_Flop d_ff_15 (.D(adder_4_y), .clk(clock_1_out), .Q(d_ff_15_q));  // open: Qn, preset, reset
  and and_18 (and_18_out, d_ff_2_q, not_3_out);
  or or_9 (or_9_out[0], and_19_out, and_23_out);
  or or_10 (or_9_out[1], and_20_out, and_24_out);
  or or_11 (or_9_out[2], and_21_out, and_25_out);
  or or_12 (or_9_out[3], and_22_out, and_26_out);
  D_Flip_Flop d_ff_16 (.D(ram_1_dout[4]), .clk(and_18_out), .Q(d_ff_16_q));  // open: Qn, preset, reset
  D_Flip_Flop d_ff_17 (.D(ram_1_dout[5]), .clk(and_18_out), .Q(d_ff_17_q));  // open: Qn, preset, reset
  D_Flip_Flop d_ff_18 (.D(ram_1_dout[6]), .clk(and_18_out), .Q(d_ff_18_q));  // open: Qn, preset, reset
  D_Flip_Flop d_ff_19 (.D(ram_1_dout[7]), .clk(and_18_out), .Q(d_ff_19_q));  // open: Qn, preset, reset
  D_Flip_Flop d_ff_20 (.D(ram_1_dout[0]), .clk(and_18_out), .Q(d_ff_20_q[0]));  // open: Qn, preset, reset
  D_Flip_Flop d_ff_21 (.D(ram_1_dout[1]), .clk(and_18_out), .Q(d_ff_20_q[1]));  // open: Qn, preset, reset
  D_Flip_Flop d_ff_22 (.D(ram_1_dout[2]), .clk(and_18_out), .Q(d_ff_20_q[2]));  // open: Qn, preset, reset
  D_Flip_Flop d_ff_23 (.D(ram_1_dout[3]), .clk(and_18_out), .Q(d_ff_20_q[3]));  // open: Qn, preset, reset
  and and_19 (and_19_out, d_ff_6_q[0], not_4_out);
  and and_20 (and_20_out, d_ff_6_q[1], not_4_out);
  and and_21 (and_21_out, d_ff_6_q[2], not_4_out);
  and and_22 (and_22_out, d_ff_6_q[3], not_4_out);
  not not_4 (not_4_out, and_28_out);
  and and_23 (and_23_out, d_ff_20_q[0], and_28_out);
  and and_24 (and_24_out, d_ff_20_q[1], and_28_out);
  and and_25 (and_25_out, d_ff_20_q[2], and_28_out);
  and and_26 (and_26_out, d_ff_20_q[3], and_28_out);
  not not_5 (not_5_out, d_ff_19_q);
  not not_6 (not_6_out, d_ff_18_q);
  not not_7 (not_7_out, d_ff_17_q);
  not not_8 (not_8_out, d_ff_16_q);
  and and_27 (_0000, not_8_out, not_7_out, execute_puls_out, not_6_out, not_5_out);
  and and_28 (and_28_out, d_ff_16_q, not_7_out, execute_puls_out, not_6_out, not_5_out);
  and and_29 (_0010, not_8_out, d_ff_17_q, execute_puls_out, not_6_out, not_5_out);
  and and_30 (_0011, d_ff_16_q, d_ff_17_q, execute_puls_out, not_6_out, not_5_out);
  and and_31 (_0100, not_8_out, not_7_out, execute_puls_out, d_ff_18_q, not_5_out);
  and and_32 (_0101, d_ff_16_q, not_7_out, execute_puls_out, d_ff_18_q, not_5_out);
  and and_33 (_0110, not_8_out, d_ff_17_q, execute_puls_out, d_ff_18_q, not_5_out);
  and and_34 (_0111, d_ff_16_q, d_ff_17_q, execute_puls_out, d_ff_18_q, not_5_out);
  and and_35 (_1000, not_8_out, not_7_out, execute_puls_out, not_6_out, d_ff_19_q);
  and and_36 (_1001, d_ff_16_q, not_7_out, execute_puls_out, not_6_out, d_ff_19_q);
  and and_37 (_1010, not_8_out, d_ff_17_q, execute_puls_out, not_6_out, d_ff_19_q);
  and and_38 (_1011, d_ff_16_q, d_ff_17_q, execute_puls_out, not_6_out, d_ff_19_q);
  and and_39 (_1100, not_8_out, not_7_out, execute_puls_out, d_ff_18_q, d_ff_19_q);
  and and_40 (_1101, d_ff_16_q, not_7_out, execute_puls_out, d_ff_18_q, d_ff_19_q);
  and and_41 (_1110, not_8_out, d_ff_17_q, execute_puls_out, d_ff_18_q, d_ff_19_q);
  and and_42 (_1111, d_ff_16_q, d_ff_17_q, execute_puls_out, d_ff_18_q, d_ff_19_q);
  LedBar #(.matrixcols(4)) ledbar_1 (
    .led0(d_ff_20_q[0]), .led1(d_ff_20_q[1]), .led2(d_ff_20_q[2]), .led3(d_ff_20_q[3]));

  // Notes on the sheet:
  //   fetch register
  //   ram page
  //   program page
  //   enable write to a register
  //   a register
  //   ram side register
  //   opcode
  //   operand
  //   Instruction register
  //   use Operand as address
  //   Operand
  //   instruction decoder
  //   LDA
endmodule

module adder (
  input  a,
  input  b,
  output x,
  output y
);

  wire and_2_out, and_3_out, not_1_out, not_2_out;

  not not_1 (not_1_out, a);
  not not_2 (not_2_out, b);
  and and_1 (x, a, b);
  and and_2 (and_2_out, a, not_2_out);
  and and_3 (and_3_out, not_1_out, b);
  or or_1 (y, and_2_out, and_3_out);
endmodule
